# Fritzing sketch continuity (saved by Fritzing 0.9.3b)
breadboards: 1

parts:
  R1 = Resistor [tolerance=±5% resistance=220 package=THT]
  LED1 = LED - 5mm [color="Red (633nm)" package="5 mm [THT]"]
  J1 = female pin header, 2 pins [form="♀ (female)"]
  J2 = female pin header, 2 pins [form="♀ (female)"]

nets:
  N1: R1.Pin_0, J1.pin1
  N2: R1.Pin_1, LED1.anode
  N3: LED1.cathode, J2.pin2
  GND: J2.pin1

notes:
  D2
  fils de test
  https://www.sla99.fr
