# Fritzing sketch multimeter (saved by Fritzing 0.9.3b)
breadboards: 1

parts:
  Composant1 = Arduino Nano (Rev3.0)
  R1 = Resistor [tolerance=±5% resistance=220 package=THT]
  R2 = Resistor [tolerance=±5% resistance=220 package=THT]
  R3 = Resistor [tolerance=±5% resistance=220 package=THT]
  R4 = Resistor [tolerance=±5% resistance=220 package=THT]
  R5 = Resistor [tolerance=±5% resistance=220 package=THT]
  R6 = Resistor [tolerance=±5% resistance=220 package=THT]
  R7 = Resistor [tolerance=±5% resistance=220 package=THT]
  U2 = 2-Channel 5v Relay Shield [package=relay-2ch5v10a]
  LED1 = LED - 5mm [color="Red (633nm)" package="5 mm [THT]"]
  J1 = Dagu DGServo 9g header connector (female) [package=THT]
  R9 = Resistor [tolerance=±5% resistance=220 package=THT]
  R10 = Resistor [tolerance=±5% resistance=220 package=THT]
  S2 = Pushbutton [package="[THT]"]
  part = Grove OLED 128x96
  R11 = Resistor [tolerance=±5% resistance=220 package=THT]

nets:
  N1: Composant1.D2, R11.Pin_1
  N2: Composant1.D3, U2.IN2
  N3: Composant1.D4, U2.IN1
  N4: Composant1.D6, R1.Pin_1
  N5: Composant1.D7, R2.Pin_1
  N6: Composant1.D8, R3.Pin_1
  N7: Composant1.D9, R4.Pin_1
  N8: Composant1.D10, R5.Pin_1
  N9: Composant1.D11/MOSI, R6.Pin_1
  N10: Composant1.D12/MISO, R7.Pin_1
  GND: Composant1.GND, U2.GND, R10.Pin_1
  5V: Composant1.5V, U2.VCC
  N11: Composant1.A6, R9.Pin_1, R10.Pin_0
  N12: Composant1.A5, part.SCL
  N13: Composant1.A4, part.SDA
  N14: Composant1.A2, S2.Pin_3, S2.Pin_4
  N15: Composant1.A1, R1.Pin_0, R2.Pin_0, R3.Pin_0, R4.Pin_0, R5.Pin_0, R6.Pin_0, R7.Pin_0, U2.K2-On
  N16: U2.K1-In, U2.K2-In, LED1.anode, J1.gnd
  N17: U2.K1-On, R9.Pin_0
  N18: LED1.cathode, R11.Pin_0

notes:
  Sortie Multimetre
  Borne -
  Borne +
  Ecran OLED 128x32
  Double Relais
  Bouton Selection
  Circuits :
  Bleu : Ohmmètre
  Violet : Continuité
  Jaune : Voltmètre
  Rouge : 5V
  Noir : GND
  https://www.sla99.fr
  220 ohms
  560 ohms
  1 kohm
  2,2 kohm
  4,7 kohm
  10 kohm
  22 kohm
  100 kohm
  220 ohm
  Marron : Relais

custom parts:
  2-Channel 5v Relay Shield: 2 Channel 5v Relay Shield w. 2x SPD-06VDC-SD-C
